# Fritzing sketch tone_02 (saved by Fritzing 0.9.3b)
breadboards: 1

parts:
  Part1 = Arduino Uno (Rev3) - ICSP
  SP1 = SPEAKER [package=pcb_mount_speaker]
  Nano1 = Arduino Nano v2.3
  SP2 = SPEAKER [package=pcb_mount_speaker]

nets:
  N1: Part1.GND, SP1.+
  N2: Part1.D5_PWM, SP1.-
  N3: Nano1.GND, SP2.+
  N4: Nano1.D5, SP2.-
